# Fritzing sketch sketch (saved by Fritzing 0.9.4)

parts:
  Composant1 = Arduino Nano (Rev3.0)
  U1 = SLIDER [package=slider]
  U2 = SLIDER [package=slider]
  M2 = DC Motor
  U3 = SLIDER [package=slider]
  M3 = DC Motor
  U4 = SLIDER [package=slider]
  M4 = DC Motor
  S1 = Pushbutton [package="[THT]"]  # not connected
  Composant2 = Adafruit TCA9548A
  OLED1 = OLED 128x64 I2C Monochrome Display
  OLED2 = OLED 128x64 I2C Monochrome Display
  OLED3 = OLED 128x64 I2C Monochrome Display
  OLED4 = OLED 128x64 I2C Monochrome Display
  U5 = L9110 H-bridge module [part_number="L9110 H-bridge"]
  M1 = DC Motor
  U6 = L9110 H-bridge module [part_number="L9110 H-bridge"]
  U7 = BATTERY-2 [package=battery-aa]
  U8 = BATTERY-2 [package=battery-aa]
  U9 = BATTERY-2 [package=battery-aa]
  U10 = BATTERY-2 [package=battery-aa]
  U11 = BATTERY-2 [package=battery-aa]
  U12 = BATTERY-2 [package=battery-aa]

nets:
  GND: Composant1.GND, U1.E, U2.E, U3.E, U4.E, Composant2.GND, Composant2.A0, Composant2.A1, Composant2.A2, U5.GND, U6.GND, U11.-1
  5V: Composant1.5V, U1.A, U2.A, U3.A, U4.A, Composant2.VCC
  N1: Composant1.A5, Composant2.INPUTSCL
  N2: Composant1.A4, Composant2.INPUTSDA
  N3: Composant1.A3, U4.S
  N4: Composant1.A2, U3.S
  N5: Composant1.A1, U2.S
  N6: Composant1.A0, U1.S
  N7: M2.pin_1, U5.MOTOR_A-B
  N8: M2.pin_2, U5.MOTOR_A-A
  N9: M3.pin_1, U6.MOTOR_B-B
  N10: M3.pin_2, U6.MOTOR_B-A
  N11: M4.pin_1, U6.MOTOR_A-B
  N12: M4.pin_2, U6.MOTOR_A-A
  N13: Composant2.2SDA, OLED2.SDA
  N14: Composant2.2SCL, OLED2.SCK
  N15: Composant2.4SDA, OLED3.SDA
  N16: Composant2.4SCL, OLED3.SCK
  N17: Composant2.6SDA, OLED4.SDA
  N18: Composant2.6SCL, OLED4.SCK
  N19: Composant2.1SDA, OLED1.SDA
  N20: Composant2.1SCL, OLED1.SCK
  VCC: U5.VCC, U6.VCC, U7.+1
  N21: U5.MOTOR_B-A, M1.pin_2
  N22: U5.MOTOR_B-B, M1.pin_1
  N23: U7.-1, U8.+1
  N24: U8.-1, U9.+1
  N25: U9.-1, U10.+1
  N26: U10.-1, U12.+1
  N27: U11.+1, U12.-1

custom parts:
  Adafruit TCA9548A: You just found the perfect I2C sensor, and you want to wire up two or three or more of them to your Arduino when you realize "Uh oh, this chip has a fixed I2C address, and from what I know about I2C, you cannot have two devices with the same address on the same SDA/SCL pins!" Are you out of luck? You would be, if you didn't have this ultra-cool TCA9548A 1-to-8 I2C multiplexer! Finally, a way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
